// Logisim project LogiClock.circ as structural Verilog: 9 circuits, main circuit main
module main (
  input  Start_Stop
);

  wire button_1_out, button_2_out, button_3_out, button_4_out, button_5_out, clock_1_out, motherboard_1_a,
       motherboard_1_alarm_led, motherboard_1_alarm_set_indicator, motherboard_1_b, motherboard_1_c,
       motherboard_1_clock_indicator, motherboard_1_countdown_indicator, motherboard_1_d, motherboard_1_e,
       motherboard_1_f, motherboard_1_g, motherboard_1_h0_a, motherboard_1_h0_b, motherboard_1_h0_c,
       motherboard_1_h0_d, motherboard_1_h0_e, motherboard_1_h0_f, motherboard_1_h0_g, motherboard_1_h1_a,
       motherboard_1_h1_b, motherboard_1_h1_c, motherboard_1_h1_d, motherboard_1_h1_e, motherboard_1_h1_f,
       motherboard_1_h1_g, motherboard_1_m0_a, motherboard_1_m0_b, motherboard_1_m0_c, motherboard_1_m0_d,
       motherboard_1_m0_e, motherboard_1_m0_f, motherboard_1_m0_g, motherboard_1_m1_a, motherboard_1_m1_b,
       motherboard_1_m1_c, motherboard_1_m1_d, motherboard_1_m1_e, motherboard_1_m1_f, motherboard_1_m1_g,
       motherboard_1_s0_a, motherboard_1_s0_b, motherboard_1_s0_c, motherboard_1_s0_d, motherboard_1_s0_e,
       motherboard_1_s0_f, motherboard_1_s0_g, motherboard_1_s1_a, motherboard_1_s1_b, motherboard_1_s1_c,
       motherboard_1_s1_d, motherboard_1_s1_e, motherboard_1_s1_f, motherboard_1_s1_g,
       motherboard_1_stopwatch_indicator, Reset_out;
  wire [1:0] slider_1_out;
  wire [5:0] motherboard_1_colon_0, motherboard_1_colon_1, motherboard_1_space_0;

  LED led_1 (.in(motherboard_1_alarm_led));
  _7_Segment_Display u_7_segment_display_1 (
    .g(motherboard_1_h1_g), .f(motherboard_1_h1_f), .a(motherboard_1_h1_a), .b(motherboard_1_h1_b),
    .e(motherboard_1_h1_e), .d(motherboard_1_h1_d), .c(motherboard_1_h1_c));  // open: dp
  Button button_1 (.out(button_1_out));
  _7_Segment_Display u_7_segment_display_2 (
    .g(motherboard_1_h0_g), .f(motherboard_1_h0_f), .a(motherboard_1_h0_a), .b(motherboard_1_h0_b),
    .e(motherboard_1_h0_e), .d(motherboard_1_h0_d), .c(motherboard_1_h0_c));  // open: dp
  _7_Segment_Display u_7_segment_display_3 (
    .g(motherboard_1_m1_g), .f(motherboard_1_m1_f), .a(motherboard_1_m1_a), .b(motherboard_1_m1_b),
    .e(motherboard_1_m1_e), .d(motherboard_1_m1_d), .c(motherboard_1_m1_c));  // open: dp
  DotMatrix #(.dotshape("clusterSegment"), .matrixcols(1), .matrixrows(6)) dotmatrix_1 (.col0(motherboard_1_colon_1));
  LED led_2 (.in(motherboard_1_clock_indicator));
  Button button_2 (.out(button_2_out));
  Button button_3 (.out(button_3_out));
  _7_Segment_Display u_7_segment_display_4 (
    .g(motherboard_1_m0_g), .f(motherboard_1_m0_f), .a(motherboard_1_m0_a), .b(motherboard_1_m0_b),
    .e(motherboard_1_m0_e), .d(motherboard_1_m0_d), .c(motherboard_1_m0_c));  // open: dp
  _7_Segment_Display u_7_segment_display_5 (
    .g(motherboard_1_s1_g), .f(motherboard_1_s1_f), .a(motherboard_1_s1_a), .b(motherboard_1_s1_b),
    .e(motherboard_1_s1_e), .d(motherboard_1_s1_d), .c(motherboard_1_s1_c));  // open: dp
  DotMatrix #(.dotshape("clusterSegment"), .matrixcols(1), .matrixrows(6)) dotmatrix_2 (.col0(motherboard_1_colon_0));
  LED led_3 (.in(motherboard_1_alarm_set_indicator));
  LED led_4 (.in(motherboard_1_stopwatch_indicator));
  Button Reset (.out(Reset_out));
  Button button_4 (.out(button_4_out));
  Button button_5 (.out(button_5_out));
  _7_Segment_Display u_7_segment_display_6 (
    .g(motherboard_1_s0_g), .f(motherboard_1_s0_f), .a(motherboard_1_s0_a), .b(motherboard_1_s0_b),
    .e(motherboard_1_s0_e), .d(motherboard_1_s0_d), .c(motherboard_1_s0_c));  // open: dp
  DotMatrix #(.dotshape("clusterSegment"), .matrixcols(1), .matrixrows(6)) dotmatrix_3 (.col0(motherboard_1_space_0));
  LED led_5 (.in(motherboard_1_countdown_indicator));
  Clock clock_1 (.out(clock_1_out));
  _7_Segment_Display u_7_segment_display_7 (
    .g(motherboard_1_a), .f(motherboard_1_b), .a(motherboard_1_c), .b(motherboard_1_d), .e(motherboard_1_e),
    .d(motherboard_1_f), .c(motherboard_1_g));  // open: dp
  // Switch switch_1: pin names not known
  Slider #(.width(2)) slider_1 (.out(slider_1_out));
  // Buzzer buzzer_1: pin names not known
  Motherboard motherboard_1 (
    .Stop_Start(Start_Stop), .Clock(clock_1_out), .Reset(Reset_out), .Slider(slider_1_out),
    .ADD_S0(button_5_out), .ADD_S1(button_4_out), .ADD_M0(button_3_out), .ADD_M1(button_2_out),
    .ADD_H(button_1_out), .M1_B(motherboard_1_m1_b), .M1_A(motherboard_1_m1_a), .M1_F(motherboard_1_m1_f),
    .M1_G(motherboard_1_m1_g), .M1_E(motherboard_1_m1_e), .M1_D(motherboard_1_m1_d),
    .M1_C(motherboard_1_m1_c), .M0_B(motherboard_1_m0_b), .M0_A(motherboard_1_m0_a),
    .M0_F(motherboard_1_m0_f), .M0_G(motherboard_1_m0_g), .M0_E(motherboard_1_m0_e),
    .M0_D(motherboard_1_m0_d), .M0_C(motherboard_1_m0_c), .S1_B(motherboard_1_s1_b),
    .S1_A(motherboard_1_s1_a), .S1_F(motherboard_1_s1_f), .S1_G(motherboard_1_s1_g),
    .S1_E(motherboard_1_s1_e), .S1_D(motherboard_1_s1_d), .S1_C(motherboard_1_s1_c), .G(motherboard_1_g),
    .F(motherboard_1_f), .E(motherboard_1_e), .D(motherboard_1_d), .C(motherboard_1_c), .B(motherboard_1_b),
    .A(motherboard_1_a), .S0_B(motherboard_1_s0_b), .S0_A(motherboard_1_s0_a), .S0_F(motherboard_1_s0_f),
    .S0_G(motherboard_1_s0_g), .S0_E(motherboard_1_s0_e), .S0_D(motherboard_1_s0_d),
    .S0_C(motherboard_1_s0_c), .Colon_1(motherboard_1_colon_1), .Colon_0(motherboard_1_colon_0),
    .Space_0(motherboard_1_space_0), .Alarm_LED(motherboard_1_alarm_led),
    .Clock_Indicator(motherboard_1_clock_indicator), .Stopwatch_Indicator(motherboard_1_stopwatch_indicator),
    .Alarm_Set_Indicator(motherboard_1_alarm_set_indicator),
    .Countdown_Indicator(motherboard_1_countdown_indicator), .H1_B(motherboard_1_h1_b),
    .H1_A(motherboard_1_h1_a), .H1_F(motherboard_1_h1_f), .H1_G(motherboard_1_h1_g),
    .H1_E(motherboard_1_h1_e), .H1_D(motherboard_1_h1_d), .H1_C(motherboard_1_h1_c),
    .H0_B(motherboard_1_h0_b), .H0_A(motherboard_1_h0_a), .H0_F(motherboard_1_h0_f),
    .H0_G(motherboard_1_h0_g), .H0_E(motherboard_1_h0_e), .H0_D(motherboard_1_h0_d), .H0_C(motherboard_1_h0_c));  // open: Format, Cons, Alarm_Frequency, Alarm_Volume, Alarm_Buzzer

  // Notes on the sheet:
  //   +1
  //   +10
  //   CLOCK MODE
  //   +1
  //   ALARM SET
  //   STOPWATCH
  //   +10
  //   +1
  //   COUNTDOWN
  //   24H
  //   12H
  //   OPERATION:
  //   Use the slider to switch between modes
  //   Reset button restarts timer from 0.
  //   to swap between 24 Hour and 12 Hour time
  //   at the top of device to select desired time 
  //   when times runs out, use reset to restart timer.
  //   1: Clock Mode - Displays the time, use the Format Switch
  //   2: Alarm Set Mode - Displays time for alarm to sound, use buttons
  //   3: Stopwatch Mode - A stopwatch, use start/stop button to control.
  //   4: Countdown Mode - Counts down from 2 minutes, sounds alarm  
endmodule

module Modulo_6 (
  input  Clock,
  input  Reset,
  output Ov,
  output [3:0] ABCD
);

  wire and_1_out, and_2_out, JK_A_qn, JK_B_qn, JK_C_qn;

  and and_1 (and_1_out, ABCD[1], ABCD[0]);
  and and_2 (and_2_out, JK_A_qn, ABCD[0]);
  J_K_Flip_Flop JK_A (
    .J(and_1_out), .K(ABCD[0]), .clk(Clock), .Q(ABCD[2]), .Qn(JK_A_qn), .reset(Reset));  // open: preset
  J_K_Flip_Flop JK_B (
    .J(and_2_out), .K(ABCD[0]), .clk(Clock), .Q(ABCD[1]), .Qn(JK_B_qn), .reset(Reset));  // open: preset
  J_K_Flip_Flop JK_C (.J(1'b1), .K(1'b1), .clk(Clock), .Q(ABCD[0]), .Qn(JK_C_qn), .reset(Reset));  // open: preset
  and and_3 (Ov, JK_C_qn, JK_B_qn, JK_A_qn);

  assign ABCD[3] = 1'b0;
endmodule

module Modulo_10 (
  input  Clock,
  input  Reset,
  output Ov,
  output [3:0] ABCD
);

  wire and_1_out, and_2_out, and_3_out, JK_A_qn, JK_B_qn, JK_C_qn, JK_D_qn;

  and and_1 (and_1_out, ABCD[2], ABCD[1], ABCD[0]);
  J_K_Flip_Flop JK_A (
    .J(and_1_out), .K(ABCD[0]), .clk(Clock), .Q(ABCD[3]), .Qn(JK_A_qn), .reset(Reset));  // open: preset
  J_K_Flip_Flop JK_B (
    .J(and_2_out), .K(and_2_out), .clk(Clock), .Q(ABCD[2]), .Qn(JK_B_qn), .reset(Reset));  // open: preset
  and and_2 (and_2_out, ABCD[1], ABCD[0]);
  and and_3 (and_3_out, JK_A_qn, JK_C_qn, ABCD[0]);
  J_K_Flip_Flop JK_C (
    .J(and_3_out), .K(ABCD[0]), .clk(Clock), .Q(ABCD[1]), .Qn(JK_C_qn), .reset(Reset));  // open: preset
  J_K_Flip_Flop JK_D (.J(1'b1), .K(1'b1), .clk(Clock), .Q(ABCD[0]), .Qn(JK_D_qn), .reset(Reset));  // open: preset
  and and_4 (Ov, JK_D_qn, JK_C_qn, JK_B_qn, JK_A_qn);
endmodule

module Modulo_24 (
  input  Clock1,
  input  Reset,
  output [3:0] ABCD_1,
  output [3:0] ABCD_10
);

  wire and_1_out, and_2_out, modulo_10_1_ov, not_1_out, not_2_out, not_3_out, not_4_out, or_1_out;

  not not_1 (not_1_out, and_2_out);
  or or_1 (or_1_out, Reset, and_2_out);
  and and_1 (and_1_out, modulo_10_1_ov, not_1_out);
  Modulo_10 modulo_10_1 (.Clock(Clock1), .Reset(or_1_out), .Ov(modulo_10_1_ov), .ABCD(ABCD_1));
  Modulo_3 modulo_3_1 (.Clock(and_1_out), .Reset(Reset), .ABCD(ABCD_10));  // open: Ov
  not not_2 (not_2_out, ABCD_1[3]);
  not not_3 (not_3_out, ABCD_1[1]);
  not not_4 (not_4_out, ABCD_1[0]);
  and and_2 (and_2_out, not_4_out, not_3_out, ABCD_1[2], not_2_out, ABCD_10[1]);
endmodule

module Modulo_3 (
  input  Clock,
  input  Reset,
  output Ov,
  output [3:0] ABCD
);

  wire JK_A_qn, JK_B_qn, not_1_out;

  J_K_Flip_Flop JK_A (
    .J(ABCD[0]), .K(not_1_out), .clk(Clock), .Q(ABCD[1]), .Qn(JK_A_qn), .reset(Reset));  // open: preset
  J_K_Flip_Flop JK_B (
    .J(JK_A_qn), .K(not_1_out), .clk(Clock), .Q(ABCD[0]), .Qn(JK_B_qn), .reset(Reset));  // open: preset
  not not_1 (not_1_out, Reset);
  and and_1 (Ov, JK_A_qn, JK_B_qn);

  assign ABCD[3:2] = 2'b00;
endmodule

module Motherboard (
  input  ADD_S0,
  input  ADD_S1,
  input  ADD_M0,
  input  ADD_M1,
  input  ADD_H,
  input  Stop_Start,
  input  Clock,
  input  Format,
  input  [1:0] Slider,
  input  Reset,
  output Alarm_LED,
  output [5:0] Colon_1,
  output [5:0] Colon_0,
  output Alarm_Buzzer,
  output Cons,
  output [5:0] Space_0,
  output [13:0] Alarm_Frequency,
  output [6:0] Alarm_Volume,
  output G,
  output Stopwatch_Indicator,
  output F,
  output E,
  output D,
  output Alarm_Set_Indicator,
  output C,
  output B,
  output A,
  output Countdown_Indicator,
  output Clock_Indicator,
  output H1_B,
  output H0_B,
  output M1_B,
  output M0_B,
  output S1_B,
  output S0_B,
  output H1_A,
  output H0_A,
  output M1_A,
  output M0_A,
  output S1_A,
  output S0_A,
  output H1_F,
  output H0_F,
  output M1_F,
  output M0_F,
  output S1_F,
  output S0_F,
  output H1_G,
  output H0_G,
  output M1_G,
  output M0_G,
  output S1_G,
  output S0_G,
  output H1_E,
  output H0_E,
  output M1_E,
  output M0_E,
  output S1_E,
  output S0_E,
  output H1_D,
  output H0_D,
  output M1_D,
  output M0_D,
  output S1_D,
  output S0_D,
  output H1_C,
  output H0_C,
  output M1_C,
  output M0_C,
  output S1_C,
  output S0_C
);

  wire Alarm_Trigger_1, Alarm_Trigger_3, and_6_out, and_8_out, comparator_1_eq, comparator_2_eq,
       comparator_3_eq, comparator_4_eq, comparator_5_eq, comparator_6_eq, comparator_7_eq, comparator_8_eq,
       comparator_9_eq, comparator_10_eq, modulo_6_1_ov, modulo_6_2_ov, modulo_6_5_ov, modulo_6_6_ov,
       modulo_6_7_ov, modulo_10_1_ov, modulo_10_2_ov, modulo_10_5_ov, modulo_10_6_ov, modulo_10_7_ov,
       not_1_out, not_2_out, not_3_out, not_4_out, not_5_out, or_1_out, or_2_out, or_3_out, Reset_0, Reset_1,
       Reset_2, Reset_3;
  wire [3:0] H0, H0_0, H0_1, H0_2, H0_12H_0, H0_12H_1, H0_24H_0, H0_24H_1, H1, H1_0, H1_1, H1_2, H1_12H_0,
       H1_12H_1, H1_24H_0, H1_24H_1, M0, M0_0, M0_1, M0_2, M0_3, M1, M1_0, M1_1, M1_2, modulo_2_1_abcd,
       modulo_6_7_abcd, modulo_10_7_abcd, S0, S0_0, S0_1, S0_2, S0_3, S1, S1_0, S1_1, S1_2, S1_3;
  wire [5:0] bit_extender_1_out;
  wire [6:0] AM_PM_0, AM_PM_1, multiplexer_11_out;

  Multiplexer #(.width(4)) multiplexer_1 (.in0(H1_24H_0), .in1(H1_12H_0), .out(H1_0), .sel(Format));
  Multiplexer #(.width(4)) multiplexer_2 (.in0(H0_24H_0), .in1(H0_12H_0), .out(H0_0), .sel(Format));
  Modulo_10 modulo_10_1 (.Clock(Clock), .Reset(Reset_0), .Ov(modulo_10_1_ov), .ABCD(S0_0));
  Modulo_6 modulo_6_1 (.Clock(modulo_10_1_ov), .Reset(Reset_0), .Ov(modulo_6_1_ov), .ABCD(S1_0));
  Modulo_10 modulo_10_2 (.Clock(modulo_6_1_ov), .Reset(Reset_0), .Ov(modulo_10_2_ov), .ABCD(M0_0));
  Modulo_6 modulo_6_2 (.Clock(modulo_10_2_ov), .Reset(Reset_0), .Ov(modulo_6_2_ov), .ABCD(M1_0));
  Modulo_24 modulo_24_1 (.Clock1(modulo_6_2_ov), .Reset(Reset_0), .ABCD_1(H0_24H_0), .ABCD_10(H1_24H_0));
  Counter_12H counter_12h_1 (
    .Clock(modulo_6_2_ov), .Reset(Reset_0), .AM_PM(AM_PM_0), .ABCD_1(H0_12H_0), .ABCD_10(H1_12H_0));
  // Probe on Slider
  not not_1 (not_1_out, Slider[0]);
  not not_2 (not_2_out, Slider[1]);
  Multiplexer #(.select(2), .width(4)) multiplexer_3 (
    .in0(H1_0), .in1(H1_1), .in2(H1_2), .out(H1), .sel(Slider));  // open: in3
  and and_1 (Stopwatch_Indicator, Slider[1], not_1_out);
  and and_2 (Alarm_Set_Indicator, Slider[0], not_2_out, Clock);
  and and_3 (Countdown_Indicator, Slider[1], Slider[0]);
  and and_4 (Clock_Indicator, not_1_out, not_2_out);
  // BCD_to_7_Segment_decoder bcd_to_7_segment_decoder_1: pin names not known; wires that end beside it: H1_G, H1_E, H1_F, H1_D, H1, H1_A, H1_C, H1_B
  Multiplexer #(.select(2), .width(4)) multiplexer_4 (
    .in0(H0_0), .in1(H0_1), .in2(H0_2), .out(H0), .sel(Slider));  // open: in3
  // BCD_to_7_Segment_decoder bcd_to_7_segment_decoder_2: pin names not known; wires that end beside it: H0_G, H0_E, H0_F, H0_D, H0, H0_A, H0_C, H0_B
  Multiplexer #(.width(4)) multiplexer_5 (.in0(H1_24H_1), .in1(H1_12H_1), .out(H1_1), .sel(Format));
  Multiplexer #(.select(2), .width(4)) multiplexer_6 (
    .in0(M1_0), .in1(M1_1), .in2(M1_2), .out(M1), .sel(Slider));  // open: in3
  Modulo_10 modulo_10_3 (.Clock(ADD_S0), .Reset(Reset_1), .ABCD(S0_1));  // open: Ov
  Modulo_6 modulo_6_3 (.Clock(ADD_S1), .Reset(Reset_1), .ABCD(S1_1));  // open: Ov
  Modulo_10 modulo_10_4 (.Clock(ADD_M0), .Reset(Reset_1), .ABCD(M0_1));  // open: Ov
  Modulo_6 modulo_6_4 (.Clock(ADD_M1), .Reset(Reset_1), .ABCD(M1_1));  // open: Ov
  Modulo_24 modulo_24_2 (.Clock1(ADD_H), .Reset(Reset_1), .ABCD_1(H0_24H_1), .ABCD_10(H1_24H_1));
  Counter_12H counter_12h_2 (.Clock(ADD_H), .Reset(Reset_1), .AM_PM(AM_PM_1), .ABCD_1(H0_12H_1), .ABCD_10(H1_12H_1));
  Multiplexer #(.width(4)) multiplexer_7 (.in0(H0_24H_1), .in1(H0_12H_1), .out(H0_1), .sel(Format));
  // BCD_to_7_Segment_decoder bcd_to_7_segment_decoder_3: pin names not known; wires that end beside it: M1_G, M1_E, M1_F, M1_D, M1, M1_A, M1_C, M1_B
  Multiplexer #(.select(2), .width(4)) multiplexer_8 (
    .in0(M0_0), .in1(M0_1), .in2(M0_2), .in3(M0_3), .out(M0), .sel(Slider));
  Comparator #(.width(4)) comparator_1 (.a(S0_0), .b(S0_1), .eq(comparator_1_eq));  // open: gt, lt
  Comparator #(.width(4)) comparator_2 (.a(S1_0), .b(S1_1), .eq(comparator_2_eq));  // open: gt, lt
  Comparator #(.width(4)) comparator_3 (.a(M0_0), .b(M0_1), .eq(comparator_3_eq));  // open: gt, lt
  Comparator #(.width(4)) comparator_4 (.a(M1_0), .b(M1_1), .eq(comparator_4_eq));  // open: gt, lt
  Comparator #(.width(4)) comparator_5 (.a(H0_24H_0), .b(H0_24H_1), .eq(comparator_5_eq));  // open: gt, lt
  Comparator #(.width(4)) comparator_6 (.a(H1_24H_0), .b(H1_24H_1), .eq(comparator_6_eq));  // open: gt, lt
  Comparator #(.width(7)) comparator_7 (.a(AM_PM_0), .b(AM_PM_1), .eq(comparator_7_eq));  // open: gt, lt
  // BCD_to_7_Segment_decoder bcd_to_7_segment_decoder_4: pin names not known; wires that end beside it: M0_G, M0_E, M0_F, M0_D, M0, M0_A, M0_C, M0_B
  Multiplexer #(.select(2), .width(4)) multiplexer_9 (
    .in0(S1_0), .in1(S1_1), .in2(S1_2), .in3(S1_3), .out(S1), .sel(Slider));
  and and_5 (Alarm_Trigger_1, comparator_1_eq, comparator_2_eq, comparator_3_eq, comparator_4_eq, comparator_5_eq, comparator_6_eq, comparator_7_eq);
  // BCD_to_7_Segment_decoder bcd_to_7_segment_decoder_5: pin names not known; wires that end beside it: S1_G, S1_E, S1_F, S1_D, S1, S1_A, S1_C, S1_B
  Pull_Resistor pull_resistor_1 (.node(Format));
  Multiplexer #(.select(2), .width(4)) multiplexer_10 (
    .in0(S0_0), .in1(S0_1), .in2(S0_2), .in3(S0_3), .out(S0), .sel(Slider));
  and and_6 (and_6_out, Clock, Stop_Start, Stopwatch_Indicator);
  not not_3 (not_3_out, Stopwatch_Indicator);
  or or_1 (or_1_out, not_3_out, Reset_2);
  // BCD_to_7_Segment_decoder bcd_to_7_segment_decoder_6: pin names not known; wires that end beside it: S0_G, S0_E, S0_F, S0_D, S0, S0_A, S0_C, S0_B
  Multiplexer #(.select(2), .width(7)) multiplexer_11 (
    .in0(AM_PM_0), .in1(AM_PM_1), .out(multiplexer_11_out), .sel(Slider));  // open: in2, in3
  Multiplexer #(.width(7)) multiplexer_12 (
    .in1(multiplexer_11_out), .out({A, B, C, D, E, F, G}), .sel(Format));  // open: in0
  Modulo_10 modulo_10_5 (.Clock(and_6_out), .Reset(or_1_out), .Ov(modulo_10_5_ov), .ABCD(S0_2));
  Modulo_6 modulo_6_5 (.Clock(modulo_10_5_ov), .Reset(or_1_out), .Ov(modulo_6_5_ov), .ABCD(S1_2));
  Modulo_10 modulo_10_6 (.Clock(modulo_6_5_ov), .Reset(or_1_out), .Ov(modulo_10_6_ov), .ABCD(M0_2));
  Modulo_6 modulo_6_6 (.Clock(modulo_10_6_ov), .Reset(or_1_out), .Ov(modulo_6_6_ov), .ABCD(M1_2));
  Modulo_24 modulo_24_3 (.Clock1(modulo_6_6_ov), .Reset(or_1_out), .ABCD_1(H0_2), .ABCD_10(H1_2));
  Demultiplexer #(.select(2)) demultiplexer_1 (
    .out0(Reset_0), .out1(Reset_1), .out2(Reset_2), .out3(Reset_3), .in(Reset), .sel(Slider));
  assign bit_extender_1_out = {{5{Clock}}, Clock};  // Bit_Extender bit_extender_1
  assign Colon_0 = bit_extender_1_out & 6'b010010;  // AND_Gate and_7, 6 bits wide
  assign Space_0 = {{5{1'b0}}, 1'b0};  // Bit_Extender bit_extender_2
  not not_4 (not_4_out, Alarm_Trigger_3);
  not not_5 (not_5_out, Countdown_Indicator);
  and and_8 (and_8_out, Clock, Stop_Start, not_4_out, Countdown_Indicator);
  or or_2 (or_2_out, not_5_out, Reset_3);
  Modulo_10 modulo_10_7 (.Clock(and_8_out), .Reset(or_2_out), .Ov(modulo_10_7_ov), .ABCD(modulo_10_7_abcd));
  Modulo_6 modulo_6_7 (.Clock(modulo_10_7_ov), .Reset(or_2_out), .Ov(modulo_6_7_ov), .ABCD(modulo_6_7_abcd));
  Modulo_2 modulo_2_1 (.Clock(modulo_6_7_ov), .Reset(or_2_out), .ABCD(modulo_2_1_abcd));  // open: Ov
  or or_3 (or_3_out, Alarm_Trigger_1, Alarm_Trigger_3);
  Subtractor #(.width(4)) subtractor_1 (.a(4'b1001), .b(modulo_10_7_abcd), .out(S0_3));  // open: bin, bout
  Subtractor #(.width(4)) subtractor_2 (.a(4'b0101), .b(modulo_6_7_abcd), .out(S1_3));  // open: bin, bout
  Subtractor #(.width(4)) subtractor_3 (.a(4'b0001), .b(modulo_2_1_abcd), .out(M0_3));  // open: bin, bout
  Comparator #(.width(4)) comparator_8 (.a(4'b0000), .b(S0_3), .eq(comparator_8_eq));  // open: gt, lt
  Comparator #(.width(4)) comparator_9 (.a(4'b0000), .b(S1_3), .eq(comparator_9_eq));  // open: gt, lt
  Comparator #(.width(4)) comparator_10 (.a(4'b0000), .b(M0_3), .eq(comparator_10_eq));  // open: gt, lt
  and and_9 (Alarm_Trigger_3, comparator_10_eq, comparator_9_eq, comparator_8_eq);
  Alarm alarm_1 (.Trigger(or_3_out), .Clock(Clock), .Alarm_Output(Alarm_Buzzer));

  assign Alarm_Frequency = 14'h600;
  assign Alarm_LED = Alarm_Buzzer;
  assign Alarm_Volume = {7{1'b1}};
  assign Colon_1 = Colon_0;
  assign Cons = 1'b1;

  // Other names for the same wires on the sheet: Countdown = Countdown_Indicator; Stopwatch = Stopwatch_Indicator
endmodule

module Modulo_2 (
  input  Clock,
  input  Reset,
  output [3:0] ABCD,
  output Ov
);

  J_K_Flip_Flop j_k_ff_1 (.J(1'b1), .K(1'b1), .clk(Clock), .Q(ABCD[0]), .Qn(Ov), .reset(Reset));  // open: preset

  assign ABCD[3:1] = 3'b000;
endmodule

module Counter_12H (
  input  Clock,
  input  Reset,
  output [6:0] AM_PM,
  output [3:0] ABCD_1,
  output [3:0] ABCD_10
);

  wire and_1_out, and_2_out, and_3_out, and_4_out, and_5_out, JK_A_q, JK_A_qn, JK_B_q, JK_B_qn, JK_C_qn,
       JK_D_qn, or_1_out;
  wire [3:0] JK_D_q, modulo_2_1_abcd;

  and and_1 (and_1_out, JK_B_q, JK_D_q[1], JK_D_q[0]);
  and and_2 (and_2_out, JK_D_q[1], JK_D_q[0]);
  and and_3 (and_3_out, JK_D_q[1], JK_D_q[0]);
  J_K_Flip_Flop JK_A (.J(and_1_out), .K(JK_B_q), .clk(Clock), .Q(JK_A_q), .Qn(JK_A_qn), .reset(Reset));  // open: preset
  J_K_Flip_Flop JK_B (
    .J(and_2_out), .K(or_1_out), .clk(Clock), .Q(JK_B_q), .Qn(JK_B_qn), .reset(Reset));  // open: preset
  or or_1 (or_1_out, JK_A_q, and_3_out);
  J_K_Flip_Flop JK_C (
    .J(JK_D_q[0]), .K(JK_D_q[0]), .clk(Clock), .Q(JK_D_q[1]), .Qn(JK_C_qn), .reset(Reset));  // open: preset
  J_K_Flip_Flop JK_D (.J(1'b1), .K(1'b1), .clk(Clock), .Q(JK_D_q[0]), .Qn(JK_D_qn), .reset(Reset));  // open: preset
  or or_2 (JK_D_q[2], JK_B_q, and_4_out);
  and and_4 (and_4_out, JK_D_qn, JK_C_qn, JK_B_qn, JK_A_qn);
  or or_3 (JK_D_q[3], JK_A_q, and_4_out);
  and and_5 (and_5_out, JK_A_q, JK_B_q);
  // Binary_to_BCD_converter binary_to_bcd_converter_1: pin names not known; wires that end beside it: 1'b0, {{5{1'b0}}, JK_D_q}, ABCD_10, ABCD_1
  Modulo_2 modulo_2_1 (.Clock(and_5_out), .Reset(Reset), .ABCD(modulo_2_1_abcd));  // open: Ov
  not not_1 (AM_PM[0], modulo_2_1_abcd[0]);

  assign AM_PM[6:1] = 6'b111110;
endmodule

module Alarm (
  input  Clock,
  input  Trigger,
  output Alarm_Output
);

  wire and_1_out, and_2_out, modulo_3_1_ov, modulo_10_1_ov, not_1_out, not_2_out;

  not not_1 (not_1_out, Trigger);
  and and_1 (and_1_out, not_1_out, and_2_out);
  Modulo_10 modulo_10_1 (.Clock(Clock), .Reset(and_1_out), .Ov(modulo_10_1_ov));  // open: ABCD
  Modulo_3 modulo_3_1 (.Clock(modulo_10_1_ov), .Ov(modulo_3_1_ov));  // open: Reset, ABCD
  and and_2 (and_2_out, modulo_10_1_ov, modulo_3_1_ov);
  not not_2 (not_2_out, and_2_out);
  and and_3 (Alarm_Output, Clock, not_2_out);
endmodule
